// Logisim project hw4.circ as structural Verilog: 11 circuits, main circuit main
module main (
  input  reset
);

  wire alu_2_beq, alu_2_bgt, and_1_out, clk_out, control_1_branchmux, control_1_immedmux, control_1_isbranch,
       control_1_jumpmux1, control_1_jumpmux2, control_1_keyboard, control_1_regmux2, control_1_regwe,
       control_1_romwe, control_1_shiftmux, control_1_tty, keyboard_1_avail, memorylatch_1_oe_latched,
       memorylatch_1_we_latched, multiplexer_5_out, not_1_out;
  wire [1:0] control_1_aluop, control_1_rdmux, control_1_regmux1;
  wire [2:0] multiplexer_2_out, splittingbits_1_rd, splittingbits_1_rs, splittingbits_1_rt,
       splittingbits_1_shamt;
  wire [3:0] splittingbits_1_opcode;
  wire [5:0] splittingbits_1_immed;
  wire [6:0] keyboard_1_data;
  wire [7:0] multiplexer_10_out;
  wire [11:0] splittingbits_1_address;
  wire [15:0] alu_1_data_out, alu_2_data_out, alu_3_data_out, bit_extender_1_out, bit_extender_2_out,
       Data_Memory_704a74f6_dout, Instruction_Memory_b2d019ad_data, memorylatch_1_address_latched,
       memorylatch_1_data_in_latched, multiplexer_1_out, multiplexer_3_out, multiplexer_4_out,
       multiplexer_6_out, multiplexer_7_out, multiplexer_8_out, multiplexer_9_out, PC_data_out,
       registerfile_1_rs1_out, registerfile_1_rs2_out, shiftleft_1_data_out, shiftright_1_data_out;

  Clock clk (.out(clk_out));
  CreateRegister PC (
    .reset(reset), .clk(clk_out), .write_en(1'b1), .data_in(multiplexer_8_out), .data_out(PC_data_out));
  TTY #(.rows(13), .cols(80), .trigger("falling")) tty_1 (
    .data(bit_extender_1_out[6:0]), .clk(clk_out), .we(control_1_tty), .clr(reset));
  ALU alu_1 (.A(PC_data_out), .B(16'h1), .Opcode(2'b00), .data_out(alu_1_data_out));  // open: beq, bgt
  ROM #(.addrWidth(16), .dataWidth(16)) Instruction_Memory_b2d019ad (
    .addr(PC_data_out), .data(Instruction_Memory_b2d019ad_data));
  Multiplexer #(.width(16), .enable("false")) multiplexer_1 (
    .in0(multiplexer_9_out), .in1(alu_1_data_out), .out(multiplexer_1_out), .sel(control_1_regmux2));
  not not_1 (not_1_out, clk_out);
  SplittingBits splittingbits_1 (
    .data_in(Instruction_Memory_b2d019ad_data), .opcode(splittingbits_1_opcode), .rs(splittingbits_1_rs),
    .rd(splittingbits_1_rd), .rt(splittingbits_1_rt), .shamt(splittingbits_1_shamt),
    .immed(splittingbits_1_immed), .address(splittingbits_1_address));
  Control control_1 (
    .opcode(splittingbits_1_opcode), .RdMUX(control_1_rdmux), .tty(control_1_tty),
    .keyboard(control_1_keyboard), .ImmedMUX(control_1_immedmux), .RegWE(control_1_regwe),
    .ALUop(control_1_aluop), .romWE(control_1_romwe), .RegMUX1(control_1_regmux1),
    .RegMUX2(control_1_regmux2), .shiftMUX(control_1_shiftmux), .branchMUX(control_1_branchmux),
    .isBranch(control_1_isbranch), .jumpMUX1(control_1_jumpmux1), .jumpMUX2(control_1_jumpmux2));
  RegisterFile registerfile_1 (
    .rd(multiplexer_2_out), .wr_enable(control_1_regwe), .data_in(multiplexer_1_out), .clk(not_1_out),
    .reset(reset), .rs1(splittingbits_1_rs), .rs2(splittingbits_1_rt), .rs2_out(registerfile_1_rs2_out),
    .rs1_out(registerfile_1_rs1_out));
  Multiplexer #(.select(2), .width(3), .enable("false")) multiplexer_2 (
    .in0(splittingbits_1_rt), .in1(splittingbits_1_rd), .in2(3'b111), .out(multiplexer_2_out),
    .sel(control_1_rdmux));  // open: in3
  assign bit_extender_1_out = {{10{splittingbits_1_immed[5]}}, splittingbits_1_immed};  // Bit_Extender bit_extender_1
  assign bit_extender_2_out = {{4{splittingbits_1_address[11]}}, splittingbits_1_address};  // Bit_Extender bit_extender_2
  ShiftLeft shiftleft_1 (
    .shamt(splittingbits_1_shamt), .data_in(registerfile_1_rs1_out), .data_out(shiftleft_1_data_out));
  ShiftRight shiftright_1 (
    .data_out(shiftright_1_data_out), .data_in(registerfile_1_rs1_out), .shamt(splittingbits_1_shamt));
  ALU alu_2 (
    .A(registerfile_1_rs1_out), .B(multiplexer_3_out), .Opcode(control_1_aluop), .data_out(alu_2_data_out),
    .beq(alu_2_beq), .bgt(alu_2_bgt));
  Multiplexer #(.width(16), .enable("false")) multiplexer_3 (
    .in0(registerfile_1_rs2_out), .in1(bit_extender_1_out), .out(multiplexer_3_out), .sel(control_1_immedmux));
  ALU alu_3 (.A(alu_1_data_out), .B(bit_extender_1_out), .Opcode(2'b00), .data_out(alu_3_data_out));  // open: beq, bgt
  Multiplexer #(.width(16), .enable("false")) multiplexer_4 (
    .in0(shiftleft_1_data_out), .in1(shiftright_1_data_out), .out(multiplexer_4_out), .sel(control_1_shiftmux));
  MemoryLatch memorylatch_1 (
    .address(alu_2_data_out), .WE(control_1_romwe), .clk(clk_out), .data_in(registerfile_1_rs2_out),
    .address_latched(memorylatch_1_address_latched), .WE_latched(memorylatch_1_we_latched),
    .OE_latched(memorylatch_1_oe_latched), .data_in_latched(memorylatch_1_data_in_latched));
  Multiplexer #(.enable("false")) multiplexer_5 (
    .in0(alu_2_bgt), .in1(alu_2_beq), .out(multiplexer_5_out), .sel(control_1_branchmux));
  RAM #(.addrWidth(16), .dataWidth(16), .trigger("high"), .databus("bibus")) Data_Memory_704a74f6 (
    .addr(memorylatch_1_address_latched), .we(memorylatch_1_we_latched), .oe(memorylatch_1_oe_latched),
    .din(memorylatch_1_data_in_latched), .dout(Data_Memory_704a74f6_dout));
  and and_1 (and_1_out, control_1_isbranch, multiplexer_5_out);
  Multiplexer #(.width(16), .enable("false")) multiplexer_6 (
    .in0(multiplexer_7_out), .in1(bit_extender_2_out), .out(multiplexer_6_out), .sel(control_1_jumpmux1));
  Multiplexer #(.width(16), .enable("false")) multiplexer_7 (
    .in0(alu_1_data_out), .in1(alu_3_data_out), .out(multiplexer_7_out), .sel(and_1_out));
  Multiplexer #(.width(16), .enable("false")) multiplexer_8 (
    .in0(multiplexer_6_out), .in1(registerfile_1_rs1_out), .out(multiplexer_8_out), .sel(control_1_jumpmux2));
  Multiplexer #(.select(2), .width(16), .enable("false")) multiplexer_9 (
    .in0(alu_2_data_out), .in1(multiplexer_4_out), .in2(Data_Memory_704a74f6_dout),
    .in3({{8{1'b0}}, multiplexer_10_out}), .out(multiplexer_9_out), .sel(control_1_regmux1));
  Keyboard #(.buflen(7)) keyboard_1 (
    .clk(clk_out), .re(control_1_keyboard), .clr(reset), .avail(keyboard_1_avail), .data(keyboard_1_data));
  Multiplexer #(.width(8), .enable("false")) multiplexer_10 (
    .in0({1'b0, keyboard_1_data}), .in1(8'h80), .out(multiplexer_10_out), .sel(keyboard_1_avail));
endmodule

module RegisterFile (
  input  [2:0] rd,
  input  wr_enable,
  input  [15:0] data_in,
  input  clk,
  input  reset,
  input  [2:0] rs1,
  input  [2:0] rs2,
  output [15:0] rs2_out,
  output [15:0] rs1_out
);

  wire decoder_1_out0, decoder_1_out1, decoder_1_out2, decoder_1_out3, decoder_1_out4, decoder_1_out5,
       decoder_1_out6, decoder_1_out7, decoder_2_out0, decoder_2_out1, decoder_2_out2, decoder_2_out3,
       decoder_2_out4, decoder_2_out5, decoder_2_out6, decoder_2_out7, decoder_3_out0, decoder_3_out1,
       decoder_3_out2, decoder_3_out3, decoder_3_out4, decoder_3_out5, decoder_3_out6, decoder_3_out7;
  wire [15:0] createregister_1_data_out, createregister_2_data_out, createregister_3_data_out,
       createregister_4_data_out, createregister_5_data_out, createregister_6_data_out,
       createregister_7_data_out, createregister_8_data_out;

  Decoder #(.select(3)) decoder_1 (
    .out0(decoder_1_out0), .out1(decoder_1_out1), .out2(decoder_1_out2), .out3(decoder_1_out3),
    .out4(decoder_1_out4), .out5(decoder_1_out5), .out6(decoder_1_out6), .out7(decoder_1_out7), .sel(rd),
    .en(wr_enable));
  CreateRegister createregister_1 (
    .reset(reset), .clk(clk), .write_en(decoder_1_out0), .data_in(data_in),
    .data_out(createregister_1_data_out));
  // Probe on createregister_1_data_out
  CreateRegister createregister_2 (
    .reset(reset), .clk(clk), .write_en(decoder_1_out1), .data_in(data_in),
    .data_out(createregister_2_data_out));
  // Probe on createregister_2_data_out
  CreateRegister createregister_3 (
    .reset(reset), .clk(clk), .write_en(decoder_1_out3), .data_in(data_in),
    .data_out(createregister_3_data_out));
  CreateRegister createregister_4 (
    .reset(reset), .clk(clk), .write_en(decoder_1_out2), .data_in(data_in),
    .data_out(createregister_4_data_out));
  // Probe on createregister_4_data_out
  CreateRegister createregister_5 (
    .reset(reset), .clk(clk), .write_en(decoder_1_out4), .data_in(data_in),
    .data_out(createregister_5_data_out));
  // Probe on createregister_3_data_out
  CreateRegister createregister_6 (
    .reset(reset), .clk(clk), .write_en(decoder_1_out5), .data_in(data_in),
    .data_out(createregister_6_data_out));
  // Probe on createregister_6_data_out
  // Probe on createregister_5_data_out
  CreateRegister createregister_7 (
    .reset(reset), .clk(clk), .write_en(decoder_1_out6), .data_in(data_in),
    .data_out(createregister_7_data_out));
  // Probe on createregister_7_data_out
  CreateRegister createregister_8 (
    .reset(reset), .clk(clk), .write_en(decoder_1_out7), .data_in(data_in),
    .data_out(createregister_8_data_out));
  // Probe on createregister_8_data_out
  Decoder #(.select(3)) decoder_2 (
    .out0(decoder_2_out0), .out1(decoder_2_out1), .out2(decoder_2_out2), .out3(decoder_2_out3),
    .out4(decoder_2_out4), .out5(decoder_2_out5), .out6(decoder_2_out6), .out7(decoder_2_out7), .sel(rs1));  // open: en
  assign rs1_out = decoder_2_out2 ? createregister_4_data_out : 16'bz;  // Controlled_Buffer controlled_buffer_1
  assign rs1_out = decoder_2_out1 ? createregister_2_data_out : 16'bz;  // Controlled_Buffer controlled_buffer_2
  assign rs1_out = decoder_2_out0 ? createregister_1_data_out : 16'bz;  // Controlled_Buffer controlled_buffer_3
  assign rs1_out = decoder_2_out6 ? createregister_7_data_out : 16'bz;  // Controlled_Buffer controlled_buffer_4
  assign rs1_out = decoder_2_out5 ? createregister_6_data_out : 16'bz;  // Controlled_Buffer controlled_buffer_5
  assign rs1_out = decoder_2_out4 ? createregister_5_data_out : 16'bz;  // Controlled_Buffer controlled_buffer_6
  assign rs1_out = decoder_2_out3 ? createregister_3_data_out : 16'bz;  // Controlled_Buffer controlled_buffer_7
  assign rs2_out = decoder_3_out2 ? createregister_4_data_out : 16'bz;  // Controlled_Buffer controlled_buffer_8
  assign rs2_out = decoder_3_out1 ? createregister_2_data_out : 16'bz;  // Controlled_Buffer controlled_buffer_9
  assign rs2_out = decoder_3_out0 ? createregister_1_data_out : 16'bz;  // Controlled_Buffer controlled_buffer_10
  assign rs1_out = decoder_2_out7 ? createregister_8_data_out : 16'bz;  // Controlled_Buffer controlled_buffer_11
  Decoder #(.select(3)) decoder_3 (
    .out0(decoder_3_out0), .out1(decoder_3_out1), .out2(decoder_3_out2), .out3(decoder_3_out3),
    .out4(decoder_3_out4), .out5(decoder_3_out5), .out6(decoder_3_out6), .out7(decoder_3_out7), .sel(rs2));  // open: en
  assign rs2_out = decoder_3_out6 ? createregister_7_data_out : 16'bz;  // Controlled_Buffer controlled_buffer_12
  assign rs2_out = decoder_3_out5 ? createregister_6_data_out : 16'bz;  // Controlled_Buffer controlled_buffer_13
  assign rs2_out = decoder_3_out4 ? createregister_5_data_out : 16'bz;  // Controlled_Buffer controlled_buffer_14
  assign rs2_out = decoder_3_out3 ? createregister_3_data_out : 16'bz;  // Controlled_Buffer controlled_buffer_15
  assign rs2_out = decoder_3_out7 ? createregister_8_data_out : 16'bz;  // Controlled_Buffer controlled_buffer_16
endmodule

module CreateRegister (
  input  reset,
  input  clk,
  input  write_en,
  input  [15:0] data_in,
  output [15:0] data_out
);

  wire and_1_out;

  and and_1 (and_1_out, clk, write_en);
  D_Flip_Flop d_ff_1 (.D(data_in[0]), .clk(and_1_out), .Q(data_out[0]), .reset(reset));  // open: Qn, preset
  D_Flip_Flop d_ff_2 (.D(data_in[1]), .clk(and_1_out), .Q(data_out[1]), .reset(reset));  // open: Qn, preset
  D_Flip_Flop d_ff_3 (.D(data_in[2]), .clk(and_1_out), .Q(data_out[2]), .reset(reset));  // open: Qn, preset
  D_Flip_Flop d_ff_4 (.D(data_in[3]), .clk(and_1_out), .Q(data_out[3]), .reset(reset));  // open: Qn, preset
  D_Flip_Flop d_ff_5 (.D(data_in[4]), .clk(and_1_out), .Q(data_out[4]), .reset(reset));  // open: Qn, preset
  D_Flip_Flop d_ff_6 (.D(data_in[5]), .clk(and_1_out), .Q(data_out[5]), .reset(reset));  // open: Qn, preset
  D_Flip_Flop d_ff_7 (.D(data_in[6]), .clk(and_1_out), .Q(data_out[6]), .reset(reset));  // open: Qn, preset
  D_Flip_Flop d_ff_8 (.D(data_in[7]), .clk(and_1_out), .Q(data_out[7]), .reset(reset));  // open: Qn, preset
  D_Flip_Flop d_ff_9 (.D(data_in[8]), .clk(and_1_out), .Q(data_out[8]), .reset(reset));  // open: Qn, preset
  D_Flip_Flop d_ff_10 (.D(data_in[9]), .clk(and_1_out), .Q(data_out[9]), .reset(reset));  // open: Qn, preset
  D_Flip_Flop d_ff_11 (.D(data_in[10]), .clk(and_1_out), .Q(data_out[10]), .reset(reset));  // open: Qn, preset
  D_Flip_Flop d_ff_12 (.D(data_in[11]), .clk(and_1_out), .Q(data_out[11]), .reset(reset));  // open: Qn, preset
  D_Flip_Flop d_ff_13 (.D(data_in[12]), .clk(and_1_out), .Q(data_out[12]), .reset(reset));  // open: Qn, preset
  D_Flip_Flop d_ff_14 (.D(data_in[13]), .clk(and_1_out), .Q(data_out[13]), .reset(reset));  // open: Qn, preset
  D_Flip_Flop d_ff_15 (.D(data_in[14]), .clk(and_1_out), .Q(data_out[14]), .reset(reset));  // open: Qn, preset
  D_Flip_Flop d_ff_16 (.D(data_in[15]), .clk(and_1_out), .Q(data_out[15]), .reset(reset));  // open: Qn, preset

  // Notes on the sheet:
  //   clk: pull=up
endmodule

module MemoryLatch (
  input  [15:0] address,
  input  WE,
  input  clk,
  input  [15:0] data_in,
  output [15:0] address_latched,
  output WE_latched,
  output OE_latched,
  output [15:0] data_in_latched
);

  wire d_ff_1_q;
  wire [15:0] register_1_q;

  Register #(.width(16), .trigger("falling")) register_1 (
    .D(address), .en(WE), .clk(clk), .Q(register_1_q));  // open: clr
  Register #(.width(16), .trigger("falling")) register_2 (
    .D(data_in), .en(WE), .clk(clk), .Q(data_in_latched));  // open: clr
  D_Flip_Flop #(.trigger("falling")) d_ff_1 (.D(WE), .clk(clk), .Q(d_ff_1_q));  // open: Qn, preset, reset
  Multiplexer #(.width(16), .enable("false")) multiplexer_1 (
    .in0(address), .in1(register_1_q), .out(address_latched), .sel(d_ff_1_q));
  and and_1 (WE_latched, clk, d_ff_1_q);
  not not_1 (OE_latched, WE_latched);
endmodule

module ALU (
  input  [15:0] A,
  input  [15:0] B,
  input  [1:0] Opcode,
  output beq,
  output bgt,
  output [15:0] data_out
);

  wire not_1_out, not_2_out;
  wire [15:0] adding_1_result, adding_2_result, and_1_out, or_1_out;

  Adding adding_1 (.sub(1'b0), .result(adding_1_result), .A(A), .B(B));
  Adding adding_2 (.sub(1'b1), .result(adding_2_result), .A(A), .B(B));
  assign and_1_out = A & B;  // AND_Gate and_1, 16 bits wide
  assign or_1_out = A | B;  // OR_Gate or_1, 16 bits wide
  Multiplexer #(.select(2), .width(16), .enable("false")) multiplexer_1 (
    .in0(adding_1_result), .in1(adding_2_result), .in2(and_1_out), .in3(or_1_out), .out(data_out),
    .sel(Opcode));
  nor nor_1 (beq, data_out[0], data_out[1], data_out[2], data_out[3], data_out[4], data_out[5], data_out[6], data_out[7], data_out[8], data_out[9], data_out[10], data_out[11], data_out[12], data_out[13], data_out[14], data_out[15]);
  not not_1 (not_1_out, beq);
  not not_2 (not_2_out, data_out[15]);
  and and_2 (bgt, not_1_out, not_2_out);
endmodule

module Control (
  input  [3:0] opcode,
  output RegWE,
  output shiftMUX,
  output tty,
  output keyboard,
  output romWE,
  output RegMUX2,
  output branchMUX,
  output jumpMUX1,
  output jumpMUX2,
  output isBranch,
  output [1:0] RegMUX1,
  output [1:0] ALUop,
  output [1:0] RdMUX,
  output ImmedMUX
);

  wire add, addi, \and , bgt, lw, \or , or_6_out, or_10_out, shl, sub;

  or or_1 (RdMUX[0], keyboard, \or , addi, \and , sub, add, shiftMUX, shl);
  Decoder #(.select(4)) decoder_1 (
    .out0(tty), .out1(keyboard), .out2(lw), .out3(romWE), .out4(branchMUX), .out5(bgt), .out6(\or ),
    .out7(\and ), .out8(addi), .out9(add), .out10(sub), .out11(shiftMUX), .out12(shl), .out13(jumpMUX1),
    .out14(RdMUX[1]), .out15(jumpMUX2), .sel(opcode));  // open: en
  or or_2 (ImmedMUX, lw, romWE, branchMUX, bgt, addi);
  or or_3 (RegWE, keyboard, lw, \or , \and , addi, add, sub, shiftMUX, shl, RdMUX[1]);
  or or_4 (ALUop[1], \or , \and );
  or or_5 (ALUop[0], \and , or_6_out);
  or or_6 (or_6_out, sub, branchMUX, bgt);
  or or_7 (isBranch, branchMUX, bgt);
  or or_8 (RegMUX1[1], lw, keyboard);
  or or_9 (RegMUX1[0], keyboard, or_10_out);
  or or_10 (or_10_out, shiftMUX, shl);

  assign RegMUX2 = RdMUX[1];

  // Other names for the same wires on the sheet: beq = branchMUX; input = keyboard; j = jumpMUX1; jr = jumpMUX2;
  //   output = tty; jal = RdMUX[1]; shra = shiftMUX; sw = romWE
endmodule

module SplittingBits (
  input  [15:0] data_in,
  output [11:0] address,
  output [3:0] opcode,
  output [2:0] rt,
  output [5:0] immed,
  output [2:0] rd,
  output [2:0] shamt,
  output [2:0] rs
);


  assign address = data_in[11:0];
  assign immed = data_in[5:0];
  assign opcode = data_in[15:12];
  assign rd = data_in[8:6];
  assign rs = data_in[11:9];
  assign rt = data_in[5:3];
  assign shamt = data_in[2:0];
endmodule

module Adding1Bit (
  input  A,
  input  B,
  input  Cin,
  output Cout,
  output Sum
);

  wire and_1_out, and_2_out, xor_1_out;

  and and_1 (and_1_out, A, B);
  xor xor_1 (xor_1_out, A, B);
  and and_2 (and_2_out, xor_1_out, Cin);
  or or_1 (Cout, and_1_out, and_2_out);
  xor xor_2 (Sum, xor_1_out, Cin);
endmodule

module Adding (
  input  [15:0] B,
  input  [15:0] A,
  input  sub,
  output [15:0] result
);

  wire adding1bit_2_cout, adding1bit_3_cout, adding1bit_4_cout, adding1bit_5_cout, adding1bit_6_cout,
       adding1bit_7_cout, adding1bit_8_cout, adding1bit_9_cout, adding1bit_10_cout, adding1bit_11_cout,
       adding1bit_12_cout, adding1bit_13_cout, adding1bit_14_cout, adding1bit_15_cout, adding1bit_16_cout,
       xor_1_out, xor_2_out, xor_3_out, xor_4_out, xor_5_out, xor_6_out, xor_7_out, xor_8_out, xor_9_out,
       xor_10_out, xor_11_out, xor_12_out, xor_13_out, xor_14_out, xor_15_out, xor_16_out;

  Adding1Bit adding1bit_1 (.A(xor_1_out), .B(A[15]), .Cin(adding1bit_2_cout), .Sum(result[15]));  // open: Cout
  xor xor_1 (xor_1_out, sub, B[15]);
  Adding1Bit adding1bit_2 (
    .A(xor_2_out), .B(A[14]), .Cin(adding1bit_3_cout), .Cout(adding1bit_2_cout), .Sum(result[14]));
  xor xor_2 (xor_2_out, sub, B[14]);
  Adding1Bit adding1bit_3 (
    .A(xor_3_out), .B(A[13]), .Cin(adding1bit_4_cout), .Cout(adding1bit_3_cout), .Sum(result[13]));
  xor xor_3 (xor_3_out, sub, B[13]);
  Adding1Bit adding1bit_4 (
    .A(xor_4_out), .B(A[12]), .Cin(adding1bit_5_cout), .Cout(adding1bit_4_cout), .Sum(result[12]));
  xor xor_4 (xor_4_out, sub, B[12]);
  Adding1Bit adding1bit_5 (
    .A(xor_6_out), .B(A[11]), .Cin(adding1bit_6_cout), .Cout(adding1bit_5_cout), .Sum(result[11]));
  xor xor_5 (xor_5_out, sub, B[10]);
  xor xor_6 (xor_6_out, sub, B[11]);
  Adding1Bit adding1bit_6 (
    .A(xor_5_out), .B(A[10]), .Cin(adding1bit_7_cout), .Cout(adding1bit_6_cout), .Sum(result[10]));
  Adding1Bit adding1bit_7 (.A(xor_7_out), .B(A[9]), .Cin(adding1bit_8_cout), .Cout(adding1bit_7_cout), .Sum(result[9]));
  xor xor_7 (xor_7_out, sub, B[9]);
  Adding1Bit adding1bit_8 (.A(xor_8_out), .B(A[8]), .Cin(adding1bit_9_cout), .Cout(adding1bit_8_cout), .Sum(result[8]));
  xor xor_8 (xor_8_out, sub, B[8]);
  Adding1Bit adding1bit_9 (
    .A(xor_9_out), .B(A[7]), .Cin(adding1bit_10_cout), .Cout(adding1bit_9_cout), .Sum(result[7]));
  xor xor_9 (xor_9_out, sub, B[7]);
  Adding1Bit adding1bit_10 (
    .A(xor_10_out), .B(A[6]), .Cin(adding1bit_11_cout), .Cout(adding1bit_10_cout), .Sum(result[6]));
  xor xor_10 (xor_10_out, sub, B[6]);
  Adding1Bit adding1bit_11 (
    .A(xor_11_out), .B(A[5]), .Cin(adding1bit_12_cout), .Cout(adding1bit_11_cout), .Sum(result[5]));
  xor xor_11 (xor_11_out, sub, B[5]);
  Adding1Bit adding1bit_12 (
    .A(xor_12_out), .B(A[4]), .Cin(adding1bit_13_cout), .Cout(adding1bit_12_cout), .Sum(result[4]));
  xor xor_12 (xor_12_out, sub, B[4]);
  Adding1Bit adding1bit_13 (
    .A(xor_13_out), .B(A[3]), .Cin(adding1bit_14_cout), .Cout(adding1bit_13_cout), .Sum(result[3]));
  xor xor_13 (xor_13_out, sub, B[3]);
  xor xor_14 (xor_14_out, sub, B[2]);
  Adding1Bit adding1bit_14 (
    .A(xor_14_out), .B(A[2]), .Cin(adding1bit_15_cout), .Cout(adding1bit_14_cout), .Sum(result[2]));
  Adding1Bit adding1bit_15 (
    .A(xor_15_out), .B(A[1]), .Cin(adding1bit_16_cout), .Cout(adding1bit_15_cout), .Sum(result[1]));
  xor xor_15 (xor_15_out, sub, B[1]);
  Adding1Bit adding1bit_16 (.A(xor_16_out), .B(A[0]), .Cin(sub), .Cout(adding1bit_16_cout), .Sum(result[0]));
  xor xor_16 (xor_16_out, sub, B[0]);

  // Other names for the same wires on the sheet: a00 = A[0]; a01 = A[1]; a02 = A[2]; a03 = A[3]; a04 = A[4];
  //   a05 = A[5]; a06 = A[6]; a07 = A[7]; a08 = A[8]; a09 = A[9]; b00 = B[0]; b01 = B[1]; b02 = B[2]; b03 = B[3];
  //   b04 = B[4]; b05 = B[5]; b06 = B[6]; b07 = B[7]; b08 = B[8]; b09 = B[9]
endmodule

module ShiftRight (
  input  [15:0] data_in,
  input  [2:0] shamt,
  output [15:0] data_out
);

  Multiplexer #(.select(3), .width(16), .enable("false")) multiplexer_1 (
    .in0(data_in), .in1({{2{data_in[15]}}, data_in[14:1]}), .in2({data_in[15], 1'b0, data_in[15:2]}),
    .in3({data_in[15], 2'b00, data_in[15:3]}), .in4({data_in[15], 3'b000, data_in[15:4]}),
    .in5({data_in[15], 4'b0000, data_in[15:5]}), .in6({data_in[15], {5{1'b0}}, data_in[15:6]}),
    .in7({data_in[15], {6{1'b0}}, data_in[15:7]}), .out(data_out), .sel(shamt));

  // Other names for the same wires on the sheet: sign = data_in[15]
endmodule

module ShiftLeft (
  input  [2:0] shamt,
  input  [15:0] data_in,
  output [15:0] data_out
);

  Multiplexer #(.select(3), .width(16), .enable("false")) multiplexer_1 (
    .in0(data_in), .in1({data_in[14:0], 1'b0}), .in2({data_in[13:0], 2'b00}), .in3({data_in[12:0], 3'b000}),
    .in4({data_in[11:0], 4'b0000}), .in5({data_in[10:0], {5{1'b0}}}), .in6({data_in[9:0], {6{1'b0}}}),
    .in7({data_in[8:0], {7{1'b0}}}), .out(data_out), .sel(shamt));
endmodule
